# Fritzing sketch Interfatare KY-008 cu Arduino UNO (saved by Fritzing 0.9.3b)

parts:
  Part1 = KY-008 Laser Transmitter Module [package="Breakout board"]
  Part2 = Arduino Uno (Rev3)

nets:
  N1: Part1.S, Part2.D10_PWM/SS
  N2: Part1.-, Part2.GND

custom parts:
  KY-008 Laser Transmitter Module: Laser Transmitter module KY-008 for Arduino, emits a dot shaped red laser beam.
